// Logisim project SAPppppp.circ as structural Verilog: 19 circuits, main circuit main
module main (
  input  in_1,
  input  in_2,
  input  in_3,
  input  [7:0] in_4,
  output [7:0] out_5,
  output [7:0] out_6,
  output [3:0] out_7,
  output [7:0] out_8,
  output [7:0] out_9,
  output [7:0] out_10,
  output out_11,
  output [7:0] out_12,
  output [7:0] out_13,
  output [15:0] out_14,
  output [7:0] out_15,
  output [7:0] out_16,
  output [7:0] out_17,
  output [7:0] out_18,
  output [7:0] out_19,
  output [7:0] out_20,
  output [7:0] out_21,
  output [7:0] out_22,
  output [7:0] out_23,
  output [7:0] out_24,
  output [7:0] out_25,
  output [3:0] out_26,
  output [7:0] out_27,
  output [3:0] out_28,
  output [7:0] out_29,
  output [7:0] out_30,
  output [7:0] out_31,
  output [7:0] out_32,
  output [7:0] out_33,
  output [7:0] out_34,
  output [3:0] out_35,
  output [7:0] out_36
);

  wire a_b, a_in, a_out, alu_out, alu_sub, and_logic_en, b_in, b_out, clk, hlt, ins_reg_in_en,
       ins_reg_out_en, mar_in_en, neg_en, neg_one_en, not_en, or_logic_en, pc_en, pc_in_en, pc_out, ram_rd,
       sram_rd, sram_wr;
  wire [7:0] debug_data, ram_1_dout;
  wire [7:4] gen_purpose_reg_1_reg_int_out;

  Hex_Digit_Display hex_digit_display_1 (.value(out_5[7:4]));  // open: dp
  Hex_Digit_Display hex_digit_display_2 (.value(out_5[3:0]));  // open: dp
  assign out_36 = in_3 ? out_5 : 8'bz;  // Controlled_Buffer controlled_buffer_1
  Hex_Digit_Display hex_digit_display_3 (.value(out_7));  // open: dp
  pc_withloader pc_withloader_1 (
    .pc_en(pc_en), .pc_in(out_5[3:0]), .pc_in_en(pc_in_en), .pc_reset(in_1), .pc_clk(clk),
    .pc_out_en(pc_out), .pc_value(out_7), .pc_out(out_5[3:0]));
  Hex_Digit_Display hex_digit_display_4 (.value(out_35));  // open: dp
  gen_purpose_reg gen_purpose_reg_1 (
    .reg_in(out_36), .reg_in_en(mar_in_en), .reg_clk(clk),
    .reg_int_out({gen_purpose_reg_1_reg_int_out, out_35}));  // open: reg_out_en, reg_out
  sram sram_1 (
    .sram_rd(sram_rd), .sram_wr(sram_wr), .sram_d_in(out_5), .mar_d_in(out_5), .mar_in_en(mar_in_en),
    .sram_clk(clk), .out_7(out_14), .sram_d_out(out_5), .l0(out_16), .l1(out_17), .l2(out_18), .l3(out_19),
    .l4(out_20), .l5(out_21), .l6(out_22), .l7(out_23), .l8(out_24), .l9(out_25), .l10(out_27), .l11(out_29),
    .l12(out_30), .l13(out_31), .l14(out_32), .l15(out_33));
  RAM #(.addrWidth(4), .trigger("falling")) ram_1 (
    .addr(out_35), .oe(ram_rd), .clk(clk), .dout(ram_1_dout));  // open: we, din
  Hex_Digit_Display hex_digit_display_5 (.value(out_5[7:4]));  // open: dp
  Hex_Digit_Display hex_digit_display_6 (.value(out_5[3:0]));  // open: dp
  assign out_5 = in_3 ? debug_data : 8'bz;  // Controlled_Buffer controlled_buffer_2
  assign debug_data = ram_rd ? ram_1_dout : 8'bz;  // Controlled_Buffer controlled_buffer_3
  Hex_Digit_Display hex_digit_display_7 (.value(out_5[3:0]));  // open: dp
  gen_purpose_reg gen_purpose_reg_2 (
    .reg_in(out_5), .reg_in_en(a_in), .reg_clk(clk), .reg_out_en(a_out), .reg_int_out(out_6), .reg_out(out_5));
  gen_purpose_reg gen_purpose_reg_3 (
    .reg_in(out_5), .reg_in_en(b_in), .reg_clk(clk), .reg_out_en(b_out), .reg_int_out(out_15), .reg_out(out_5));
  ir ir_1 (
    .ins_reg_in(out_5), .ins_reg_in_en(ins_reg_in_en), .clk(clk), .ins_reg_out_en(ins_reg_out_en),
    .add_outs(out_5[3:0]), .ins_out(out_28));
  Hex_Digit_Display hex_digit_display_8 (.value(out_28));  // open: dp
  Hex_Digit_Display hex_digit_display_9 (.value(out_6[7:4]));  // open: dp
  Hex_Digit_Display hex_digit_display_10 (.value(out_6[3:0]));  // open: dp
  alu2 alu2_1 (
    .alu_in_1(out_6), .alu_out_en(alu_out), .alu_sub(alu_sub), .alu_in_2(out_15), .alu_out(out_5));  // open: alu_carry_out
  Hex_Digit_Display hex_digit_display_11 (.value(out_15[7:4]));  // open: dp
  Hex_Digit_Display hex_digit_display_12 (.value(out_15[3:0]));  // open: dp
  control_sequence control_sequence_1 (
    .clk(clk), .clk_reset(in_2), .ins_msb(out_28), .debug(in_3), .pc_in_en(pc_in_en), .pc_en(pc_en),
    .pc_out_final(pc_out), .ram_rd(ram_rd), .b_in(b_in), .mar_in_en_final(mar_in_en),
    .and_logic_en(and_logic_en), .hlt(hlt), .or_logic_en(or_logic_en), .a_out_final(a_out),
    .b_out_final(b_out), .alu_out(alu_out), .alu_sub(alu_sub), .neg_en(neg_en), .neg_one_en(neg_one_en),
    .ins_reg_out_en(ins_reg_out_en), .a_in(a_in), .a_b(a_b), .not_en(not_en), .sram_rd_final(sram_rd),
    .ins_reg_in_en(ins_reg_in_en), .sram_wr_final(sram_wr));
  LED led_1 (.in(in_3));
  Clock clock_1 (.out(clk));
  and_logic and_logic_1 (.logic_a_in(out_6), .logic_b_in(out_15), .and_logic_en(and_logic_en), .out_4(out_5));
  or_logic or_logic_1 (.logic_a_in(out_6), .logic_b_in(out_15), .or_logic_en(or_logic_en), .out_4(out_5));
  not_logic not_logic_1 (
    .in_1(in_4), .neg_one_en(neg_one_en), .neg_en(neg_en), .not_en(not_en), .a_b(a_b), .not_a_in(out_6),
    .not_b_in(out_15), .neg_out(out_9), .neg_cout(out_11), .inv(out_12), .invert(out_5));

  assign out_8 = out_5;
  assign out_10 = out_5;
  assign out_13 = out_5;
  assign out_26 = out_5[3:0];
  assign out_34 = out_5;

  // Other names for the same wires on the sheet: debug = in_3; debug_data_out[7:0] = out_5; neg[7:0] = in_4;
  //   pc_reset = in_1; ring_reset = in_2

  // Notes on the sheet:
  //   Data Bus
  //   Counter Value
  //   Loader Counter Value
  //   instruction opcode
  //   instruction opcode
  //   Reg A
  //   Reg B
  //   Code loading mode LED
endmodule

module gen_purpose_reg (
  input  [7:0] reg_in,
  input  reg_in_en,
  input  reg_clk,
  input  reg_out_en,
  output [7:0] reg_int_out,
  output [7:0] reg_out
);

  wire multiplexer_1_out, multiplexer_2_out, multiplexer_3_out, multiplexer_4_out, multiplexer_5_out,
       multiplexer_6_out, multiplexer_7_out, multiplexer_8_out;

  Multiplexer multiplexer_1 (.in0(reg_int_out[7]), .in1(reg_in[7]), .out(multiplexer_1_out), .sel(reg_in_en));
  D_Flip_Flop d_ff_1 (.D(multiplexer_1_out), .clk(reg_clk), .Q(reg_int_out[7]));  // open: Qn, preset, reset
  assign reg_out[7] = reg_out_en ? reg_int_out[7] : 1'bz;  // Controlled_Buffer controlled_buffer_1
  Multiplexer multiplexer_2 (.in0(reg_int_out[6]), .in1(reg_in[6]), .out(multiplexer_2_out), .sel(reg_in_en));
  D_Flip_Flop d_ff_2 (.D(multiplexer_2_out), .clk(reg_clk), .Q(reg_int_out[6]));  // open: Qn, preset, reset
  Multiplexer multiplexer_3 (.in0(reg_int_out[5]), .in1(reg_in[5]), .out(multiplexer_3_out), .sel(reg_in_en));
  assign reg_out[6] = reg_out_en ? reg_int_out[6] : 1'bz;  // Controlled_Buffer controlled_buffer_2
  D_Flip_Flop d_ff_3 (.D(multiplexer_3_out), .clk(reg_clk), .Q(reg_int_out[5]));  // open: Qn, preset, reset
  Multiplexer multiplexer_4 (.in0(reg_int_out[4]), .in1(reg_in[4]), .out(multiplexer_4_out), .sel(reg_in_en));
  assign reg_out[5] = reg_out_en ? reg_int_out[5] : 1'bz;  // Controlled_Buffer controlled_buffer_3
  D_Flip_Flop d_ff_4 (.D(multiplexer_4_out), .clk(reg_clk), .Q(reg_int_out[4]));  // open: Qn, preset, reset
  Multiplexer multiplexer_5 (.in0(reg_int_out[3]), .in1(reg_in[3]), .out(multiplexer_5_out), .sel(reg_in_en));
  assign reg_out[4] = reg_out_en ? reg_int_out[4] : 1'bz;  // Controlled_Buffer controlled_buffer_4
  D_Flip_Flop d_ff_5 (.D(multiplexer_5_out), .clk(reg_clk), .Q(reg_int_out[3]));  // open: Qn, preset, reset
  assign reg_out[3] = reg_out_en ? reg_int_out[3] : 1'bz;  // Controlled_Buffer controlled_buffer_5
  Multiplexer multiplexer_6 (.in0(reg_int_out[2]), .in1(reg_in[2]), .out(multiplexer_6_out), .sel(reg_in_en));
  D_Flip_Flop d_ff_6 (.D(multiplexer_6_out), .clk(reg_clk), .Q(reg_int_out[2]));  // open: Qn, preset, reset
  assign reg_out[2] = reg_out_en ? reg_int_out[2] : 1'bz;  // Controlled_Buffer controlled_buffer_6
  Multiplexer multiplexer_7 (.in0(reg_int_out[1]), .in1(reg_in[1]), .out(multiplexer_7_out), .sel(reg_in_en));
  D_Flip_Flop d_ff_7 (.D(multiplexer_7_out), .clk(reg_clk), .Q(reg_int_out[1]));  // open: Qn, preset, reset
  Multiplexer multiplexer_8 (.in0(reg_int_out[0]), .in1(reg_in[0]), .out(multiplexer_8_out), .sel(reg_in_en));
  assign reg_out[1] = reg_out_en ? reg_int_out[1] : 1'bz;  // Controlled_Buffer controlled_buffer_7
  D_Flip_Flop d_ff_8 (.D(multiplexer_8_out), .clk(reg_clk), .Q(reg_int_out[0]));  // open: Qn, preset, reset
  assign reg_out[0] = reg_out_en ? reg_int_out[0] : 1'bz;  // Controlled_Buffer controlled_buffer_8
endmodule

module alu2 (
  input  [7:0] alu_in_1,
  input  alu_out_en,
  input  alu_sub,
  input  [7:0] alu_in_2,
  output alu_carry_out,
  output [7:0] alu_out
);

  wire adder_2_cout, adder_3_cout, adder_4_cout, adder_5_cout, adder_6_cout, adder_7_cout, adder_8_cout,
       xor_1_out, xor_2_out, xor_3_out, xor_4_out, xor_5_out, xor_6_out, xor_7_out, xor_8_out;
  wire [7:0] adder_8_out;

  xor xor_1 (xor_1_out, alu_in_2[7], alu_sub);
  Adder #(.width(1)) adder_1 (
    .a(alu_in_1[7]), .b(xor_1_out), .out(adder_8_out[7]), .cin(adder_2_cout), .cout(alu_carry_out));
  xor xor_2 (xor_2_out, alu_in_2[6], alu_sub);
  Adder #(.width(1)) adder_2 (
    .a(alu_in_1[6]), .b(xor_2_out), .out(adder_8_out[6]), .cin(adder_3_cout), .cout(adder_2_cout));
  xor xor_3 (xor_3_out, alu_in_2[5], alu_sub);
  Adder #(.width(1)) adder_3 (
    .a(alu_in_1[5]), .b(xor_3_out), .out(adder_8_out[5]), .cin(adder_4_cout), .cout(adder_3_cout));
  xor xor_4 (xor_4_out, alu_in_2[4], alu_sub);
  Adder #(.width(1)) adder_4 (
    .a(alu_in_1[4]), .b(xor_4_out), .out(adder_8_out[4]), .cin(adder_5_cout), .cout(adder_4_cout));
  xor xor_5 (xor_5_out, alu_in_2[3], alu_sub);
  Adder #(.width(1)) adder_5 (
    .a(alu_in_1[3]), .b(xor_5_out), .out(adder_8_out[3]), .cin(adder_6_cout), .cout(adder_5_cout));
  xor xor_6 (xor_6_out, alu_in_2[2], alu_sub);
  Adder #(.width(1)) adder_6 (
    .a(alu_in_1[2]), .b(xor_6_out), .out(adder_8_out[2]), .cin(adder_7_cout), .cout(adder_6_cout));
  xor xor_7 (xor_7_out, alu_in_2[1], alu_sub);
  Adder #(.width(1)) adder_7 (
    .a(alu_in_1[1]), .b(xor_7_out), .out(adder_8_out[1]), .cin(adder_8_cout), .cout(adder_7_cout));
  xor xor_8 (xor_8_out, alu_in_2[0], alu_sub);
  Adder #(.width(1)) adder_8 (.a(alu_in_1[0]), .b(xor_8_out), .out(adder_8_out[0]), .cin(alu_sub), .cout(adder_8_cout));
  assign alu_out = alu_out_en ? adder_8_out : 8'bz;  // Controlled_Buffer controlled_buffer_1
endmodule

module program_counter (
  input  pc_en,
  input  pc_clk,
  input  pc_reset,
  input  pc_out_en,
  output [3:0] pc_value,
  output [3:0] pc_out
);

  wire j_k_ff_2_qn, j_k_ff_3_qn, j_k_ff_4_qn;

  J_K_Flip_Flop j_k_ff_1 (
    .J(pc_en), .K(pc_en), .clk(j_k_ff_2_qn), .Q(pc_value[3]), .reset(pc_reset));  // open: Qn, preset
  J_K_Flip_Flop j_k_ff_2 (
    .J(pc_en), .K(pc_en), .clk(j_k_ff_3_qn), .Q(pc_value[2]), .Qn(j_k_ff_2_qn), .reset(pc_reset));  // open: preset
  J_K_Flip_Flop j_k_ff_3 (
    .J(pc_en), .K(pc_en), .clk(j_k_ff_4_qn), .Q(pc_value[1]), .Qn(j_k_ff_3_qn), .reset(pc_reset));  // open: preset
  J_K_Flip_Flop j_k_ff_4 (
    .J(pc_en), .K(pc_en), .clk(pc_clk), .Q(pc_value[0]), .Qn(j_k_ff_4_qn), .reset(pc_reset));  // open: preset
  assign pc_out = pc_out_en ? pc_value : 4'bz;  // Controlled_Buffer controlled_buffer_1
endmodule

module dec_4to16 (
  input  [3:0] dec_sel,
  output [15:0] dec_out
);

  wire not_1_out, not_2_out, not_3_out, not_4_out;

  not not_1 (not_1_out, dec_sel[3]);
  not not_2 (not_2_out, dec_sel[2]);
  not not_3 (not_3_out, dec_sel[1]);
  not not_4 (not_4_out, dec_sel[0]);
  and and_1 (dec_out[0], not_4_out, not_3_out, not_2_out, not_1_out);
  and and_2 (dec_out[1], dec_sel[0], not_3_out, not_2_out, not_1_out);
  and and_3 (dec_out[2], not_4_out, dec_sel[1], not_2_out, not_1_out);
  and and_4 (dec_out[3], dec_sel[0], dec_sel[1], not_2_out, not_1_out);
  and and_5 (dec_out[4], not_4_out, not_3_out, dec_sel[2], not_1_out);
  and and_6 (dec_out[5], dec_sel[0], not_3_out, dec_sel[2], not_1_out);
  and and_7 (dec_out[6], not_4_out, dec_sel[1], dec_sel[2], not_1_out);
  and and_8 (dec_out[7], dec_sel[0], dec_sel[1], dec_sel[2], not_1_out);
  and and_9 (dec_out[8], not_4_out, not_3_out, not_2_out, dec_sel[3]);
  and and_10 (dec_out[9], dec_sel[0], not_3_out, not_2_out, dec_sel[3]);
  and and_11 (dec_out[10], not_4_out, dec_sel[1], not_2_out, dec_sel[3]);
  and and_12 (dec_out[11], dec_sel[0], dec_sel[1], not_2_out, dec_sel[3]);
  and and_13 (dec_out[12], not_4_out, not_3_out, dec_sel[2], dec_sel[3]);
  and and_14 (dec_out[13], dec_sel[0], not_3_out, dec_sel[2], dec_sel[3]);
  and and_15 (dec_out[14], not_4_out, dec_sel[1], dec_sel[2], dec_sel[3]);
  and and_16 (dec_out[15], dec_sel[0], dec_sel[1], dec_sel[2], dec_sel[3]);
endmodule

module sram_cell (
  input  [7:0] data_in,
  input  wr_en,
  input  clk,
  input  cs,
  input  rd_en,
  output [7:0] memory_content,
  output [7:0] data_out
);

  wire and_1_out, and_2_out;

  and and_1 (and_1_out, wr_en, cs);
  and and_2 (and_2_out, cs, rd_en);
  gen_purpose_reg gen_purpose_reg_1 (
    .reg_in(data_in), .reg_in_en(and_1_out), .reg_clk(clk), .reg_out_en(and_2_out),
    .reg_int_out(memory_content), .reg_out(data_out));
endmodule

module sram (
  input  sram_rd,
  input  sram_wr,
  input  [7:0] sram_d_in,
  input  [7:0] mar_d_in,
  input  mar_in_en,
  input  sram_clk,
  output [15:0] out_7,
  output [7:0] sram_d_out,
  output [7:0] l0,
  output [7:0] l1,
  output [7:0] l2,
  output [7:0] l3,
  output [7:0] l4,
  output [7:0] l5,
  output [7:0] l6,
  output [7:0] l7,
  output [7:0] l8,
  output [7:0] l9,
  output [7:0] l10,
  output [7:0] l11,
  output [7:0] l12,
  output [7:0] l13,
  output [7:0] l14,
  output [7:0] l15
);

  wire [7:0] controlled_buffer_1_out, gen_purpose_reg_1_reg_int_out;

  gen_purpose_reg gen_purpose_reg_1 (
    .reg_in(mar_d_in), .reg_in_en(mar_in_en), .reg_clk(sram_clk), .reg_int_out(gen_purpose_reg_1_reg_int_out));  // open: reg_out_en, reg_out
  dec_4to16 dec_4to16_1 (.dec_sel(gen_purpose_reg_1_reg_int_out[3:0]), .dec_out(out_7));
  assign controlled_buffer_1_out = sram_wr ? sram_d_in : 8'bz;  // Controlled_Buffer controlled_buffer_1
  sram_cell sram_cell_1 (
    .data_in(controlled_buffer_1_out), .wr_en(sram_wr), .clk(sram_clk), .cs(out_7[0]), .rd_en(sram_rd),
    .memory_content(l0), .data_out(controlled_buffer_1_out));
  sram_cell sram_cell_2 (
    .data_in(controlled_buffer_1_out), .wr_en(sram_wr), .clk(sram_clk), .cs(out_7[1]), .rd_en(sram_rd),
    .memory_content(l1), .data_out(controlled_buffer_1_out));
  sram_cell sram_cell_3 (
    .data_in(controlled_buffer_1_out), .wr_en(sram_wr), .clk(sram_clk), .cs(out_7[2]), .rd_en(sram_rd),
    .memory_content(l2), .data_out(controlled_buffer_1_out));
  sram_cell sram_cell_4 (
    .data_in(controlled_buffer_1_out), .wr_en(sram_wr), .clk(sram_clk), .cs(out_7[3]), .rd_en(sram_rd),
    .memory_content(l3), .data_out(controlled_buffer_1_out));
  sram_cell sram_cell_5 (
    .data_in(controlled_buffer_1_out), .wr_en(sram_wr), .clk(sram_clk), .cs(out_7[4]), .rd_en(sram_rd),
    .memory_content(l4), .data_out(controlled_buffer_1_out));
  sram_cell sram_cell_6 (
    .data_in(controlled_buffer_1_out), .wr_en(sram_wr), .clk(sram_clk), .cs(out_7[5]), .rd_en(sram_rd),
    .memory_content(l5), .data_out(controlled_buffer_1_out));
  sram_cell sram_cell_7 (
    .data_in(controlled_buffer_1_out), .wr_en(sram_wr), .clk(sram_clk), .cs(out_7[6]), .rd_en(sram_rd),
    .memory_content(l6), .data_out(controlled_buffer_1_out));
  sram_cell sram_cell_8 (
    .data_in(controlled_buffer_1_out), .wr_en(sram_wr), .clk(sram_clk), .cs(out_7[7]), .rd_en(sram_rd),
    .memory_content(l7), .data_out(controlled_buffer_1_out));
  sram_cell sram_cell_9 (
    .data_in(controlled_buffer_1_out), .wr_en(sram_wr), .clk(sram_clk), .cs(out_7[8]), .rd_en(sram_rd),
    .memory_content(l8), .data_out(controlled_buffer_1_out));
  sram_cell sram_cell_10 (
    .data_in(controlled_buffer_1_out), .wr_en(sram_wr), .clk(sram_clk), .cs(out_7[9]), .rd_en(sram_rd),
    .memory_content(l9), .data_out(controlled_buffer_1_out));
  sram_cell sram_cell_11 (
    .data_in(controlled_buffer_1_out), .wr_en(sram_wr), .clk(sram_clk), .cs(out_7[10]), .rd_en(sram_rd),
    .memory_content(l10), .data_out(controlled_buffer_1_out));
  sram_cell sram_cell_12 (
    .data_in(controlled_buffer_1_out), .wr_en(sram_wr), .clk(sram_clk), .cs(out_7[11]), .rd_en(sram_rd),
    .memory_content(l11), .data_out(controlled_buffer_1_out));
  sram_cell sram_cell_13 (
    .data_in(controlled_buffer_1_out), .wr_en(sram_wr), .clk(sram_clk), .cs(out_7[12]), .rd_en(sram_rd),
    .memory_content(l12), .data_out(controlled_buffer_1_out));
  sram_cell sram_cell_14 (
    .data_in(controlled_buffer_1_out), .wr_en(sram_wr), .clk(sram_clk), .cs(out_7[13]), .rd_en(sram_rd),
    .memory_content(l13), .data_out(controlled_buffer_1_out));
  sram_cell sram_cell_15 (
    .data_in(controlled_buffer_1_out), .wr_en(sram_wr), .clk(sram_clk), .cs(out_7[14]), .rd_en(sram_rd),
    .memory_content(l14), .data_out(controlled_buffer_1_out));
  sram_cell sram_cell_16 (
    .data_in(controlled_buffer_1_out), .wr_en(sram_wr), .clk(sram_clk), .cs(out_7[15]), .rd_en(sram_rd),
    .memory_content(l15), .data_out(controlled_buffer_1_out));
  assign sram_d_out = sram_rd ? controlled_buffer_1_out : 8'bz;  // Controlled_Buffer controlled_buffer_2
endmodule

module ir (
  input  [7:0] ins_reg_in,
  input  ins_reg_in_en,
  input  clk,
  input  ins_reg_out_en,
  output [3:0] add_outs,
  output [3:0] ins_out
);

  wire [3:0] gen_purpose_reg_1_reg_int_out;

  gen_purpose_reg gen_purpose_reg_1 (
    .reg_in(ins_reg_in), .reg_in_en(ins_reg_in_en), .reg_clk(clk),
    .reg_int_out({ins_out, gen_purpose_reg_1_reg_int_out}));  // open: reg_out_en, reg_out
  assign add_outs = ins_reg_out_en ? gen_purpose_reg_1_reg_int_out : 4'bz;  // Controlled_Buffer controlled_buffer_1
endmodule

module rc (
  input  rc_en,
  input  clk,
  input  ring_reset,
  output T1,
  output T2,
  output T3,
  output T4,
  output T5,
  output T6
);

  wire controlled_buffer_1_out, not_1_out;
  wire [3:0] program_counter_1_pc_value;
  wire [7:0] dec_4to16_1_dec_out_2;
  wire [7:6] dec_4to16_1_dec_out;

  assign controlled_buffer_1_out = ring_reset ? ring_reset : 1'bz;  // Controlled_Buffer controlled_buffer_1
  assign controlled_buffer_1_out = not_1_out ? dec_4to16_1_dec_out[6] : 1'bz;  // Controlled_Buffer controlled_buffer_2
  not not_1 (not_1_out, ring_reset);
  program_counter program_counter_1 (
    .pc_en(rc_en), .pc_clk(clk), .pc_reset(controlled_buffer_1_out), .pc_out_en(rc_en),
    .pc_value(program_counter_1_pc_value));  // open: pc_out
  dec_4to16 dec_4to16_1 (
    .dec_sel(program_counter_1_pc_value),
    .dec_out({dec_4to16_1_dec_out_2, dec_4to16_1_dec_out, T6, T5, T4, T3, T2, T1}));
endmodule

module ins_dec (
  input  [3:0] ir_msb,
  output isDebug,
  output isLDA,
  output isLDB,
  output isOUT,
  output isSTA,
  output and_logic,
  output or_logic,
  output neg_a,
  output neg_b,
  output not_a,
  output not_b,
  output jmp,
  output sub,
  output isHLT
);

  wire [14:13] dec_4to16_1_dec_out;

  dec_4to16 dec_4to16_1 (
    .dec_sel(ir_msb),
    .dec_out({isHLT, dec_4to16_1_dec_out, sub, jmp, not_b, not_a, neg_b, neg_a, or_logic, and_logic, isSTA, isOUT, isLDB, isLDA, isDebug}));
endmodule

module control_sequence (
  input  clk,
  input  clk_reset,
  input  [3:0] ins_msb,
  input  debug,
  output pc_in_en,
  output pc_en,
  output pc_out_final,
  output ram_rd,
  output b_in,
  output mar_in_en_final,
  output and_logic_en,
  output hlt,
  output or_logic_en,
  output a_out_final,
  output b_out_final,
  output alu_out,
  output alu_sub,
  output neg_en,
  output neg_one_en,
  output ins_reg_out_en,
  output a_in,
  output a_b,
  output not_en,
  output sram_rd_final,
  output ins_reg_in_en,
  output sram_wr_final
);

  wire and_1_out, and_2_out, and_3_out, and_4_out, and_5_out, and_6_out, and_7_out, and_8_out, and_9_out,
       and_10_out, and_11_out, and_12_out, and_13_out, and_14_out, and_15_out, and_16_out, and_17_out,
       and_18_out, and_19_out, and_20_out, and_21_out, and_22_out, and_23_out, and_24_out, and_25_out,
       and_26_out, and_28_out, and_29_out, and_32_out, and_33_out, and_34_out, and_35_out, and_36_out,
       and_37_out, and_38_out, and_39_out, and_45_out, and_46_out, and_47_out, and_48_out, and_49_out,
       and_50_out, and_51_out, and_52_out, and_53_out, and_54_out, and_55_out, and_56_out, and_57_out,
       and_58_out, and_59_out, and_60_out, and_61_out, and_62_out, and_63_out, and_65_out, and_66_out,
       and_67_out, and_68_out, and_69_out, and_70_out, and_71_out, controlled_buffer_1_out,
       demultiplexer_3_out1, ins_dec_1_and_logic, ins_dec_1_isdebug, ins_dec_1_ishlt, ins_dec_1_islda,
       ins_dec_1_isldb, ins_dec_1_isout, ins_dec_1_issta, ins_dec_1_jmp, ins_dec_1_neg_a, ins_dec_1_neg_b,
       ins_dec_1_not_a, ins_dec_1_not_b, ins_dec_1_or_logic, ins_dec_1_sub, not_1_out, or_1_out, or_3_out,
       or_5_out, or_8_out, or_12_out, pull_resistor_1_node, rc_1_t2, rc_1_t3, rc_1_t4, rc_1_t5, rc_1_t6,
       ring_reset;
  wire [3:0] multiplexer_1_out, pull_resistor_2_node;

  Pull_Resistor #(.pull(1)) pull_resistor_1 (.node(pull_resistor_1_node));
  assign controlled_buffer_1_out = not_1_out ? ring_reset : 1'bz;  // Controlled_Buffer controlled_buffer_1
  not not_1 (not_1_out, clk_reset);
  assign controlled_buffer_1_out = clk_reset ? clk_reset : 1'bz;  // Controlled_Buffer controlled_buffer_2
  Pull_Resistor pull_resistor_2 (.node(pull_resistor_2_node));
  Multiplexer #(.width(4)) multiplexer_1 (
    .in0(ins_msb), .in1(pull_resistor_2_node), .out(multiplexer_1_out), .sel(debug));
  rc rc_1 (
    .rc_en(pull_resistor_1_node), .clk(clk), .ring_reset(controlled_buffer_1_out), .T1(pc_out_final),
    .T2(rc_1_t2), .T3(rc_1_t3), .T4(rc_1_t4), .T5(rc_1_t5), .T6(rc_1_t6));
  ins_dec ins_dec_1 (
    .ir_msb(multiplexer_1_out), .isDebug(ins_dec_1_isdebug), .isLDA(ins_dec_1_islda),
    .isLDB(ins_dec_1_isldb), .isOUT(ins_dec_1_isout), .isSTA(ins_dec_1_issta),
    .and_logic(ins_dec_1_and_logic), .or_logic(ins_dec_1_or_logic), .neg_a(ins_dec_1_neg_a),
    .neg_b(ins_dec_1_neg_b), .not_a(ins_dec_1_not_a), .not_b(ins_dec_1_not_b), .jmp(ins_dec_1_jmp),
    .sub(ins_dec_1_sub), .isHLT(ins_dec_1_ishlt));
  and and_1 (and_1_out, ins_dec_1_jmp, rc_1_t3);
  Demultiplexer demultiplexer_1 (.out0(pc_en), .out1(pc_in_en), .in(rc_1_t3), .sel(and_1_out));
  and and_2 (and_2_out, ins_dec_1_islda, rc_1_t4);
  or or_1 (or_1_out, and_6_out, and_5_out, pc_out_final, and_2_out, and_7_out, and_3_out, and_4_out, and_8_out, and_9_out);
  and and_3 (and_3_out, ins_dec_1_isldb, rc_1_t4);
  or or_2 (mar_in_en_final, or_1_out, and_11_out, and_12_out, and_10_out);
  and and_4 (and_4_out, ins_dec_1_issta, rc_1_t4);
  and and_5 (and_5_out, ins_dec_1_isout, rc_1_t3);
  and and_6 (and_6_out, ins_dec_1_and_logic, rc_1_t4);
  and and_7 (and_7_out, ins_dec_1_or_logic, rc_1_t4);
  and and_8 (and_8_out, ins_dec_1_not_a, rc_1_t4);
  and and_9 (and_9_out, ins_dec_1_not_b, rc_1_t4);
  and and_10 (and_10_out, ins_dec_1_sub, rc_1_t3);
  and and_11 (and_11_out, rc_1_t4, ins_dec_1_neg_a);
  and and_12 (and_12_out, rc_1_t4, ins_dec_1_neg_b);
  or or_3 (or_3_out, rc_1_t2, and_13_out, and_14_out);
  Demultiplexer demultiplexer_2 (.out0(sram_rd_final), .out1(ram_rd), .in(or_3_out), .sel(debug));
  and and_13 (and_13_out, rc_1_t5, ins_dec_1_islda);
  and and_14 (and_14_out, rc_1_t5, ins_dec_1_isldb);
  Demultiplexer demultiplexer_3 (.out0(ins_reg_in_en), .out1(demultiplexer_3_out1), .in(rc_1_t2), .sel(debug));
  and and_15 (and_15_out, rc_1_t4, ins_dec_1_islda);
  and and_16 (and_16_out, rc_1_t4, ins_dec_1_isldb);
  or or_4 (ins_reg_out_en, and_22_out, and_16_out, and_15_out, or_5_out, and_23_out, and_20_out, and_17_out, and_21_out, and_24_out);
  and and_17 (and_17_out, rc_1_t4, ins_dec_1_issta);
  and and_18 (and_18_out, rc_1_t3, ins_dec_1_isout);
  and and_19 (and_19_out, rc_1_t3, ins_dec_1_sub);
  and and_20 (and_20_out, ins_dec_1_and_logic, rc_1_t4);
  and and_21 (and_21_out, ins_dec_1_or_logic, rc_1_t4);
  and and_22 (and_22_out, ins_dec_1_not_a, rc_1_t4);
  and and_23 (and_23_out, ins_dec_1_not_b, rc_1_t4);
  and and_24 (and_24_out, ins_dec_1_jmp, rc_1_t3);
  and and_25 (and_25_out, rc_1_t4, ins_dec_1_neg_a);
  or or_5 (or_5_out, and_18_out, and_25_out, and_26_out, and_19_out);
  and and_26 (and_26_out, rc_1_t4, ins_dec_1_neg_b);
  and and_27 (a_in, rc_1_t5, ins_dec_1_islda);
  and and_28 (and_28_out, rc_1_t5, ins_dec_1_issta);
  and and_29 (and_29_out, rc_1_t4, ins_dec_1_sub);
  buf or_6 (a_out_final, and_28_out);  // OR_Gate
  and and_30 (b_in, rc_1_t5, ins_dec_1_isldb);
  // AND_Gate and_31 is placed but not wired
  and and_32 (and_32_out, rc_1_t4, ins_dec_1_isout);
  and and_33 (and_33_out, rc_1_t4, ins_dec_1_sub);
  or or_7 (alu_out, and_32_out, and_33_out);
  or or_8 (or_8_out, and_29_out, and_39_out, and_34_out, demultiplexer_3_out1, and_37_out, and_36_out, and_35_out, and_38_out);
  and and_34 (and_34_out, rc_1_t5, ins_dec_1_issta);
  and and_35 (and_35_out, ins_dec_1_isout, rc_1_t4);
  buf or_9 (sram_wr_final, or_8_out);  // OR_Gate
  and and_36 (and_36_out, ins_dec_1_and_logic, rc_1_t5);
  and and_37 (and_37_out, ins_dec_1_or_logic, rc_1_t5);
  and and_38 (and_38_out, ins_dec_1_not_a, rc_1_t5);
  and and_39 (and_39_out, ins_dec_1_not_b, rc_1_t5);
  // AND_Gate and_40 has open pins: in0=ins_dec_1_neg_a, in1=rc_1_t6, out=open
  // AND_Gate and_41 has open pins: in0=ins_dec_1_neg_b, in1=rc_1_t6, out=open
  and and_42 (hlt, ins_dec_1_ishlt, rc_1_t4);
  and and_43 (or_logic_en, rc_1_t5, ins_dec_1_or_logic);
  and and_44 (and_logic_en, rc_1_t5, ins_dec_1_and_logic);
  and and_45 (and_45_out, ins_dec_1_not_a, rc_1_t5);
  and and_46 (and_46_out, ins_dec_1_not_b, rc_1_t5);
  or or_10 (not_en, and_45_out, and_47_out, and_48_out, and_46_out);
  and and_47 (and_47_out, ins_dec_1_neg_a, rc_1_t5);
  and and_48 (and_48_out, ins_dec_1_neg_b, rc_1_t5);
  and and_49 (and_49_out, ins_dec_1_not_b, rc_1_t5);
  and and_50 (and_50_out, rc_1_t5, ins_dec_1_neg_b);
  or or_11 (a_b, and_49_out, and_50_out);
  and and_51 (and_51_out, ins_dec_1_islda, rc_1_t6);
  and and_52 (and_52_out, ins_dec_1_isldb, rc_1_t6);
  or or_12 (or_12_out, and_57_out, and_54_out, and_51_out, and_53_out, and_58_out, and_55_out, and_52_out, and_56_out, and_59_out);
  or or_13 (ring_reset, or_12_out, and_62_out, and_61_out, and_65_out, and_60_out);
  and and_53 (and_53_out, ins_dec_1_isout, rc_1_t5);
  and and_54 (and_54_out, ins_dec_1_isdebug, rc_1_t4);
  and and_55 (and_55_out, ins_dec_1_or_logic, rc_1_t6);
  and and_56 (and_56_out, ins_dec_1_and_logic, rc_1_t6);
  and and_57 (and_57_out, ins_dec_1_not_b, rc_1_t6);
  and and_58 (and_58_out, ins_dec_1_not_a, rc_1_t6);
  and and_59 (and_59_out, ins_dec_1_jmp, rc_1_t4);
  and and_60 (and_60_out, rc_1_t5, ins_dec_1_sub);
  and and_61 (and_61_out, ins_dec_1_issta, rc_1_t6);
  and and_62 (and_62_out, ins_dec_1_neg_b, rc_1_t6);
  and and_63 (and_63_out, ins_dec_1_neg_a, rc_1_t6);
  and and_64 (alu_sub, ins_dec_1_sub, rc_1_t4);
  and and_65 (and_65_out, ins_dec_1_neg_a, rc_1_t6);
  and and_66 (and_66_out, ins_dec_1_neg_a, rc_1_t5);
  or or_14 (neg_en, and_66_out, and_63_out, and_67_out);
  and and_67 (and_67_out, ins_dec_1_neg_b, rc_1_t5);
  and and_68 (and_68_out, ins_dec_1_neg_a, rc_1_t5);
  and and_69 (and_69_out, ins_dec_1_neg_b, rc_1_t5);
  or or_15 (neg_one_en, and_68_out, and_70_out, and_69_out);
  and and_70 (and_70_out, rc_1_t6, ins_dec_1_neg_a);
  and and_71 (and_71_out, ins_dec_1_neg_b, rc_1_t6);
endmodule

module ins_loader (
  input  il_reset,
  input  il_en,
  input  clk,
  input  debug,
  output [3:0] il_address,
  output l1,
  output l2
);

  wire controlled_buffer_1_out, d_ff_1_q, not_1_out;

  Counter #(.max('hf), .width(4)) counter_1 (
    .clr(il_reset), .load(1'b0), .up(1'b1), .count(il_en), .clk(clk), .Q(il_address));  // open: D, carry
  assign controlled_buffer_1_out = debug ? not_1_out : 1'bz;  // Controlled_Buffer controlled_buffer_1
  D_Flip_Flop d_ff_1 (.D(controlled_buffer_1_out), .clk(clk), .Q(d_ff_1_q));  // open: Qn, preset, reset
  not not_1 (not_1_out, d_ff_1_q);
  and and_1 (l1, debug, not_1_out);
  and and_2 (l2, debug, d_ff_1_q);
endmodule

module pc_withloader (
  input  pc_en,
  input  [3:0] pc_in,
  input  pc_in_en,
  input  pc_reset,
  input  pc_clk,
  input  pc_out_en,
  output [3:0] pc_value,
  output [3:0] pc_out
);

  wire and_1_out, and_2_out, and_3_out, multiplexer_1_out, multiplexer_2_out, multiplexer_3_out,
       multiplexer_4_out, multiplexer_5_out, multiplexer_6_out, multiplexer_7_out, multiplexer_8_out,
       not_1_out, not_2_out, not_3_out, not_4_out;

  Multiplexer multiplexer_1 (.in0(and_1_out), .in1(not_1_out), .out(multiplexer_1_out), .sel(pc_in_en));
  and and_1 (and_1_out, pc_en, pc_value[2], pc_value[1], pc_value[0]);
  not not_1 (not_1_out, pc_in[3]);
  Multiplexer multiplexer_2 (.in0(and_1_out), .in1(pc_in[3]), .out(multiplexer_2_out), .sel(pc_in_en));
  J_K_Flip_Flop j_k_ff_1 (
    .J(multiplexer_2_out), .K(multiplexer_1_out), .clk(pc_clk), .Q(pc_value[3]), .reset(pc_reset));  // open: Qn, preset
  and and_2 (and_2_out, pc_en, pc_value[1], pc_value[0]);
  Multiplexer multiplexer_3 (.in0(and_2_out), .in1(pc_in[2]), .out(multiplexer_3_out), .sel(pc_in_en));
  Multiplexer multiplexer_4 (.in0(and_2_out), .in1(not_2_out), .out(multiplexer_4_out), .sel(pc_in_en));
  J_K_Flip_Flop j_k_ff_2 (
    .J(multiplexer_3_out), .K(multiplexer_4_out), .clk(pc_clk), .Q(pc_value[2]), .reset(pc_reset));  // open: Qn, preset
  not not_2 (not_2_out, pc_in[2]);
  and and_3 (and_3_out, pc_en, pc_value[0]);
  Multiplexer multiplexer_5 (.in0(and_3_out), .in1(pc_in[1]), .out(multiplexer_5_out), .sel(pc_in_en));
  not not_3 (not_3_out, pc_in[1]);
  Multiplexer multiplexer_6 (.in0(and_3_out), .in1(not_3_out), .out(multiplexer_6_out), .sel(pc_in_en));
  J_K_Flip_Flop j_k_ff_3 (
    .J(multiplexer_5_out), .K(multiplexer_6_out), .clk(pc_clk), .Q(pc_value[1]), .reset(pc_reset));  // open: Qn, preset
  J_K_Flip_Flop j_k_ff_4 (
    .J(multiplexer_7_out), .K(multiplexer_8_out), .clk(pc_clk), .Q(pc_value[0]), .reset(pc_reset));  // open: Qn, preset
  not not_4 (not_4_out, pc_in[0]);
  Multiplexer multiplexer_7 (.in0(pc_en), .in1(pc_in[0]), .out(multiplexer_7_out), .sel(pc_in_en));
  Multiplexer multiplexer_8 (.in0(pc_en), .in1(not_4_out), .out(multiplexer_8_out), .sel(pc_in_en));
  assign pc_out = pc_out_en ? pc_value : 4'bz;  // Controlled_Buffer controlled_buffer_1
endmodule

module backup (
  input  in_1,
  input  in_2,
  input  in_3,
  input  in_4,
  input  in_5,
  input  in_6,
  input  in_7,
  input  [7:0] in_8,
  input  in_9,
  output [7:0] out_10,
  output [3:0] out_11,
  output [7:0] out_12,
  output [7:0] out_13,
  output [7:0] out_14,
  output [7:0] out_15,
  output [7:0] out_16,
  output [7:0] out_17,
  output [7:0] out_18,
  output [7:0] out_19,
  output [7:0] out_20,
  output [7:0] out_21,
  output [7:0] out_22,
  output [7:0] out_23,
  output [7:0] out_24,
  output [3:0] out_25,
  output [7:0] out_26,
  output [3:0] out_27,
  output [7:0] out_28,
  output [7:0] out_29,
  output [7:0] out_30,
  output [7:0] out_31,
  output [7:0] out_32
);

  wire a_in, a_out, alu_out, b_in, hlt, ins_reg_in_en, ins_reg_out_en, mar_in_en, pc_en, pc_out, sram_rd,
       sram_wr;
  wire [15:8] sram_1_out_7;

  program_counter program_counter_1 (
    .pc_en(pc_en), .pc_clk(in_1), .pc_reset(in_2), .pc_out_en(pc_out), .pc_value(out_11), .pc_out(out_12[3:0]));
  sram sram_1 (
    .sram_rd(sram_rd), .sram_wr(sram_wr), .sram_d_in(out_12), .mar_d_in(out_12), .mar_in_en(mar_in_en),
    .sram_clk(in_1), .out_7({sram_1_out_7, out_12}), .sram_d_out(out_13), .l0(out_15), .l1(out_16),
    .l2(out_17), .l3(out_18), .l4(out_19), .l5(out_20), .l6(out_21), .l7(out_22), .l8(out_23), .l9(out_24),
    .l10(out_26), .l11(out_28), .l12(out_29), .l13(out_30), .l14(out_31));  // open: l15
  assign out_12 = in_3 ? in_8 : 8'bz;  // Controlled_Buffer controlled_buffer_1
  gen_purpose_reg gen_purpose_reg_1 (
    .reg_in(out_12), .reg_in_en(a_in), .reg_clk(in_1), .reg_out_en(a_out), .reg_int_out(out_10),
    .reg_out(out_12));
  gen_purpose_reg gen_purpose_reg_2 (
    .reg_in(out_12), .reg_in_en(b_in), .reg_clk(in_1), .reg_out_en(in_7), .reg_int_out(out_14),
    .reg_out(out_12));
  ir ir_1 (
    .ins_reg_in(out_12), .ins_reg_in_en(ins_reg_in_en), .clk(in_1), .ins_reg_out_en(ins_reg_out_en),
    .add_outs(out_12[3:0]), .ins_out(out_27));
  alu2 alu2_1 (
    .alu_in_1(out_10), .alu_out_en(alu_out), .alu_sub(in_9), .alu_in_2(out_14), .alu_out(out_12));  // open: alu_carry_out
  // control_sequence control_sequence_1: pin names not known; wires that end beside it: in_5, in_1, in_2, out_27, in_4, in_3, in_6, pc_out, ins_reg_in_en, b_in, hlt, pc_en, mar_in_en, sram_rd, ins_reg_out_en, a_in, a_out, alu_out, sram_wr
  // Pins of 8 and 16 bits meet at {sram_1_out_7, out_12}

  assign out_25 = out_12[3:0];
  assign out_32 = out_12;

  // Other names for the same wires on the sheet: alu_sub = in_9; b_out = in_7; clk = in_1; cs_en = in_5; debug = in_3;
  //   debug_data[7:0] = in_8; mar_in_en_manual = in_4; pc_reset = in_2; sram_wr_manual = in_6
endmodule

module and_logic (
  input  [7:0] logic_a_in,
  input  [7:0] logic_b_in,
  input  and_logic_en,
  output [7:0] out_4
);

  wire [7:0] and_8_out;

  assign out_4 = and_logic_en ? and_8_out : 8'bz;  // Controlled_Buffer controlled_buffer_1
  and and_1 (and_8_out[7], logic_a_in[7], logic_b_in[7]);
  and and_2 (and_8_out[6], logic_a_in[6], logic_b_in[6]);
  and and_3 (and_8_out[5], logic_a_in[5], logic_b_in[5]);
  and and_4 (and_8_out[4], logic_a_in[4], logic_b_in[4]);
  and and_5 (and_8_out[3], logic_a_in[3], logic_b_in[3]);
  and and_6 (and_8_out[2], logic_a_in[2], logic_b_in[2]);
  and and_7 (and_8_out[1], logic_a_in[1], logic_b_in[1]);
  and and_8 (and_8_out[0], logic_a_in[0], logic_b_in[0]);
endmodule

module or_logic (
  input  [7:0] logic_a_in,
  input  [7:0] logic_b_in,
  input  or_logic_en,
  output [7:0] out_4
);

  wire [7:0] or_8_out;

  assign out_4 = or_logic_en ? or_8_out : 8'bz;  // Controlled_Buffer controlled_buffer_1
  or or_1 (or_8_out[7], logic_a_in[7], logic_b_in[7]);
  or or_2 (or_8_out[6], logic_a_in[6], logic_b_in[6]);
  or or_3 (or_8_out[5], logic_a_in[5], logic_b_in[5]);
  or or_4 (or_8_out[4], logic_a_in[4], logic_b_in[4]);
  or or_5 (or_8_out[3], logic_a_in[3], logic_b_in[3]);
  or or_6 (or_8_out[2], logic_a_in[2], logic_b_in[2]);
  or or_7 (or_8_out[1], logic_a_in[1], logic_b_in[1]);
  or or_8 (or_8_out[0], logic_a_in[0], logic_b_in[0]);
endmodule

module not_logic (
  input  [7:0] in_1,
  input  neg_one_en,
  input  neg_en,
  input  not_en,
  input  a_b,
  input  [7:0] not_a_in,
  input  [7:0] not_b_in,
  output [7:0] neg_out,
  output neg_cout,
  output [7:0] inv,
  output [7:0] invert
);

  wire adder_1_cout, pull_resistor_1_node;
  wire [7:0] adder_1_out, demultiplexer_1_out0, demultiplexer_1_out1, multiplexer_1_out, neg, not_1_out;

  assign neg = neg_one_en ? in_1 : 8'bz;  // Controlled_Buffer controlled_buffer_1
  assign not_1_out = ~multiplexer_1_out;  // NOT_Gate not_1, 8 bits wide
  Multiplexer #(.width(8)) multiplexer_1 (.in0(not_a_in), .in1(not_b_in), .out(multiplexer_1_out), .sel(a_b));
  Pull_Resistor pull_resistor_1 (.node(pull_resistor_1_node));
  Adder adder_1 (.a(neg), .b(demultiplexer_1_out1), .out(adder_1_out), .cin(pull_resistor_1_node), .cout(adder_1_cout));
  Demultiplexer #(.width(8)) demultiplexer_1 (
    .out0(demultiplexer_1_out0), .out1(demultiplexer_1_out1), .in(not_1_out), .sel(neg_en));
  assign neg_cout = not_en ? adder_1_cout : 1'bz;  // Controlled_Buffer controlled_buffer_2
  assign inv = not_en ? demultiplexer_1_out1 : 8'bz;  // Controlled_Buffer controlled_buffer_3
  assign invert = not_en ? demultiplexer_1_out0 : 8'bz;  // Controlled_Buffer controlled_buffer_4
  assign neg_out = not_en ? adder_1_out : 8'bz;  // Controlled_Buffer controlled_buffer_5
endmodule

module main1 (
  input  in_1,
  input  in_2,
  input  in_3,
  input  [7:0] in_4,
  output [7:0] out_5,
  output [7:0] out_6,
  output [7:0] out_7,
  output [7:0] out_8,
  output [3:0] out_9,
  output [7:0] out_10,
  output neg_cout,
  output [7:0] out_12,
  output [7:0] out_13,
  output [15:0] out_14,
  output [7:0] out_15,
  output [7:0] out_16,
  output [7:0] out_17,
  output [7:0] out_18,
  output [7:0] out_19,
  output [7:0] out_20,
  output [7:0] out_21,
  output [7:0] out_22,
  output [7:0] out_23,
  output [7:0] out_24,
  output [7:0] out_25,
  output [3:0] out_26,
  output [7:0] out_27,
  output [3:0] out_28,
  output [7:0] out_29,
  output [7:0] out_30,
  output [7:0] out_31,
  output [7:0] out_32,
  output [7:0] out_33,
  output [7:0] out_34,
  output [3:0] out_35,
  output [7:0] out_36
);

  wire a_b, a_in, a_out, alu_out, alu_sub, and_logic_en, b_in, b_out, clk, hlt, ins_reg_in_en,
       ins_reg_out_en, mar_in_en, neg_en, neg_one_en, not_en, or_logic_en, pc_en, pc_in_en, pc_out, ram_rd,
       sram_rd, sram_wr;
  wire [7:0] debug_data, ram_1_dout;
  wire [7:4] gen_purpose_reg_1_reg_int_out;

  Hex_Digit_Display hex_digit_display_1 (.value(out_6[7:4]));  // open: dp
  Hex_Digit_Display hex_digit_display_2 (.value(out_6[3:0]));  // open: dp
  assign out_36 = in_3 ? out_6 : 8'bz;  // Controlled_Buffer controlled_buffer_1
  Hex_Digit_Display hex_digit_display_3 (.value(out_9));  // open: dp
  pc_withloader pc_withloader_1 (
    .pc_en(pc_en), .pc_in(out_6[3:0]), .pc_in_en(pc_in_en), .pc_reset(in_1), .pc_clk(clk),
    .pc_out_en(pc_out), .pc_value(out_9), .pc_out(out_6[3:0]));
  sram sram_1 (
    .sram_rd(sram_rd), .sram_wr(sram_wr), .sram_d_in(out_6), .mar_d_in(out_6), .mar_in_en(mar_in_en),
    .sram_clk(clk), .out_7(out_14), .sram_d_out(out_6), .l0(out_16), .l1(out_17), .l2(out_18), .l3(out_19),
    .l4(out_20), .l5(out_21), .l6(out_22), .l7(out_23), .l8(out_24), .l9(out_25), .l10(out_27), .l11(out_29),
    .l12(out_30), .l13(out_31), .l14(out_32), .l15(out_33));
  Hex_Digit_Display hex_digit_display_4 (.value(out_6[7:4]));  // open: dp
  Hex_Digit_Display hex_digit_display_5 (.value(out_6[3:0]));  // open: dp
  assign out_6 = in_3 ? debug_data : 8'bz;  // Controlled_Buffer controlled_buffer_2
  gen_purpose_reg gen_purpose_reg_1 (
    .reg_in(out_36), .reg_in_en(mar_in_en), .reg_clk(clk),
    .reg_int_out({gen_purpose_reg_1_reg_int_out, out_35}));  // open: reg_out_en, reg_out
  Hex_Digit_Display hex_digit_display_6 (.value(out_35));  // open: dp
  RAM #(.addrWidth(4), .trigger("falling")) ram_1 (
    .addr(out_35), .oe(ram_rd), .clk(clk), .dout(ram_1_dout));  // open: we, din
  gen_purpose_reg gen_purpose_reg_2 (
    .reg_in(out_6), .reg_in_en(a_in), .reg_clk(clk), .reg_out_en(a_out), .reg_int_out(out_5), .reg_out(out_6));
  gen_purpose_reg gen_purpose_reg_3 (
    .reg_in(out_6), .reg_in_en(b_in), .reg_clk(clk), .reg_out_en(b_out), .reg_int_out(out_15), .reg_out(out_6));
  Hex_Digit_Display hex_digit_display_7 (.value(out_28));  // open: dp
  ir ir_1 (
    .ins_reg_in(out_6), .ins_reg_in_en(ins_reg_in_en), .clk(clk), .ins_reg_out_en(ins_reg_out_en),
    .add_outs(out_6[3:0]), .ins_out(out_28));
  Hex_Digit_Display hex_digit_display_8 (.value(out_6[3:0]));  // open: dp
  assign debug_data = ram_rd ? ram_1_dout : 8'bz;  // Controlled_Buffer controlled_buffer_3
  Hex_Digit_Display hex_digit_display_9 (.value(out_15[7:4]));  // open: dp
  Hex_Digit_Display hex_digit_display_10 (.value(out_5[7:4]));  // open: dp
  Hex_Digit_Display hex_digit_display_11 (.value(out_5[3:0]));  // open: dp
  Hex_Digit_Display hex_digit_display_12 (.value(out_15[3:0]));  // open: dp
  LED led_1 (.in(in_3));
  alu alu_1 (
    .alu_in_1(out_5), .alu_out_en(alu_out), .alu_sub(alu_sub), .alu_in_2(out_15),
    .and_logic_en(and_logic_en), .or_logic_en(or_logic_en), .neg(in_4), .neg_one_en(neg_one_en),
    .neg_en(neg_en), .not_en(not_en), .a_b(a_b), .alu_out(out_6), .and_out(out_6), .or_out(out_6),
    .neg_out(out_10), .neg_cout(neg_cout), .inv(out_12), .invert(out_6));  // open: alu_carry_out
  control_sequence control_sequence_1 (
    .clk(clk), .clk_reset(in_2), .ins_msb(out_28), .debug(in_3), .pc_in_en(pc_in_en), .pc_en(pc_en),
    .pc_out_final(pc_out), .ram_rd(ram_rd), .b_in(b_in), .mar_in_en_final(mar_in_en),
    .and_logic_en(and_logic_en), .hlt(hlt), .or_logic_en(or_logic_en), .a_out_final(a_out),
    .b_out_final(b_out), .alu_out(alu_out), .alu_sub(alu_sub), .neg_en(neg_en), .neg_one_en(neg_one_en),
    .ins_reg_out_en(ins_reg_out_en), .a_in(a_in), .a_b(a_b), .not_en(not_en), .sram_rd_final(sram_rd),
    .ins_reg_in_en(ins_reg_in_en), .sram_wr_final(sram_wr));
  Clock clock_1 (.out(clk));

  assign out_7 = out_6;
  assign out_8 = out_6;
  assign out_13 = out_6;
  assign out_26 = out_6[3:0];
  assign out_34 = out_6;

  // Other names for the same wires on the sheet: debug = in_3; debug_data_out[7:0] = out_6; neg[7:0] = in_4;
  //   pc_reset = in_1; ring_reset = in_2

  // Notes on the sheet:
  //   Counter Value
  //   Data Bus
  //   Loader Counter Value
  //   instruction opcode
  //   instruction operand
  //   REG B
  //   REG A
  //   Code loading mode LED
  //   neg_out
endmodule

module alu (
  input  [7:0] alu_in_1,
  input  alu_out_en,
  input  alu_sub,
  input  [7:0] alu_in_2,
  input  and_logic_en,
  input  or_logic_en,
  input  [7:0] neg,
  input  neg_one_en,
  input  neg_en,
  input  not_en,
  input  a_b,
  output alu_carry_out,
  output [7:0] alu_out,
  output [7:0] and_out,
  output [7:0] or_out,
  output [7:0] neg_out,
  output neg_cout,
  output [7:0] inv,
  output [7:0] invert
);

  wire adder_2_cout, adder_3_cout, adder_4_cout, adder_5_cout, adder_6_cout, adder_7_cout, adder_8_cout,
       xor_1_out, xor_2_out, xor_3_out, xor_4_out, xor_5_out, xor_6_out, xor_7_out, xor_8_out;
  wire [7:0] adder_8_out;

  xor xor_1 (xor_1_out, alu_in_2[7], alu_sub);
  Adder #(.width(1)) adder_1 (
    .a(alu_in_1[7]), .b(xor_1_out), .out(adder_8_out[7]), .cin(adder_2_cout), .cout(alu_carry_out));
  xor xor_2 (xor_2_out, alu_in_2[6], alu_sub);
  Adder #(.width(1)) adder_2 (
    .a(alu_in_1[6]), .b(xor_2_out), .out(adder_8_out[6]), .cin(adder_3_cout), .cout(adder_2_cout));
  xor xor_3 (xor_3_out, alu_in_2[5], alu_sub);
  Adder #(.width(1)) adder_3 (
    .a(alu_in_1[5]), .b(xor_3_out), .out(adder_8_out[5]), .cin(adder_4_cout), .cout(adder_3_cout));
  xor xor_4 (xor_4_out, alu_in_2[4], alu_sub);
  Adder #(.width(1)) adder_4 (
    .a(alu_in_1[4]), .b(xor_4_out), .out(adder_8_out[4]), .cin(adder_5_cout), .cout(adder_4_cout));
  xor xor_5 (xor_5_out, alu_in_2[3], alu_sub);
  and_logic and_logic_1 (.logic_a_in(alu_in_1), .logic_b_in(alu_in_2), .and_logic_en(and_logic_en), .out_4(and_out));
  or_logic or_logic_1 (.logic_a_in(alu_in_1), .logic_b_in(alu_in_2), .or_logic_en(or_logic_en), .out_4(or_out));
  not_logic not_logic_1 (
    .in_1(neg), .neg_one_en(neg_one_en), .neg_en(neg_en), .not_en(not_en), .a_b(a_b), .not_a_in(alu_in_1),
    .not_b_in(alu_in_2), .neg_out(neg_out), .neg_cout(neg_cout), .inv(inv), .invert(invert));
  Adder #(.width(1)) adder_5 (
    .a(alu_in_1[3]), .b(xor_5_out), .out(adder_8_out[3]), .cin(adder_6_cout), .cout(adder_5_cout));
  xor xor_6 (xor_6_out, alu_in_2[2], alu_sub);
  Adder #(.width(1)) adder_6 (
    .a(alu_in_1[2]), .b(xor_6_out), .out(adder_8_out[2]), .cin(adder_7_cout), .cout(adder_6_cout));
  xor xor_7 (xor_7_out, alu_in_2[1], alu_sub);
  Adder #(.width(1)) adder_7 (
    .a(alu_in_1[1]), .b(xor_7_out), .out(adder_8_out[1]), .cin(adder_8_cout), .cout(adder_7_cout));
  xor xor_8 (xor_8_out, alu_in_2[0], alu_sub);
  Adder #(.width(1)) adder_8 (.a(alu_in_1[0]), .b(xor_8_out), .out(adder_8_out[0]), .cin(alu_sub), .cout(adder_8_cout));
  assign alu_out = alu_out_en ? adder_8_out : 8'bz;  // Controlled_Buffer controlled_buffer_1
endmodule
